# Fritzing sketch UnoPico0207 (saved by Fritzing 0.9.4)
circuit board: 19.2009cm x 10.2121cm

parts:
  元件1 = UnoPico Fritz Part
  元件2 = NeoPixel Stick [part_number=1426]
  LCD1 = TFT 1.8 inch 160x128 w SD
  Mod1 = Raspberry Pi Pico

nets:
  N1: 元件1.TX0, 元件2.DATAIN, Mod1.pin_1
  VCC: 元件1.VCC, 元件2.+5V, LCD1.pin_1, LCD1.pin_8
  GND: 元件1.GND, 元件2.GND, LCD1.pin2
  N2: 元件1.RST, LCD1.pin4
  N3: 元件1.NSS, LCD1.pin3
  N4: 元件1.NA7_LCD_CD, LCD1.pin_5
  N5: 元件1.NMOSI, LCD1.pin_6
  N6: 元件1.NSCK, LCD1.pin_7
  N7: Mod1.pin_33, Mod1.pin_38

custom parts:
  UnoPico Fritz Part: UnoPicoNanoQ
  NeoPixel Stick: Make your own little LED strip arrangement with this stick of NeoPixel LEDs. We crammed 8 of the tiny 5050 (5mm x 5mm) smart RGB LEDs onto a PCB with mounting holes and a chainable design. Use only one microcontroller pin to control as many as you can chain together! Each LED is addressable as the driver chip is inside the LED. Each one has ~18mA constant current drive so the color will be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
  TFT 1.8 inch 160x128 w SD: This is a generic 1.8 tft spi lcd display available on ebay and others. The 1.8" display has 128x160 color pixels and in this version pin names in breadboard (unlike the real board).
  Raspberry Pi Pico: Raspberry Pi Pico. Based around the RP2040 microcontroller the Pico is a low cost microcontroller device bringing Raspberry Pi quality, cost, and easy of use to the microcontroller space. Jan 2021, Split part in to two versions: tht (this one) and SMD. This one will drill holes for a .1 in header in pcb to allow plugging in the module as well as providing pads to solder the module to the top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
